// Logisim project JK - FLIP FLOP USING NAND GATES.circ as structural Verilog: 1 circuit, main circuit main
module main (
  input  J,
  input  K
);

  wire CLOCK_out, NAND_2_out, NAND_3_out, NAND_4_out, NAND_out;

  Clock CLOCK (.out(CLOCK_out));
  nand NAND (NAND_out, NAND_4_out, J, CLOCK_out);
  nand NAND_2 (NAND_2_out, CLOCK_out, K, NAND_3_out);
  nand NAND_3 (NAND_3_out, NAND_out, NAND_4_out);
  nand NAND_4 (NAND_4_out, NAND_3_out, NAND_2_out);
  LED led_1 (.in(NAND_3_out));
  LED led_2 (.in(NAND_4_out));

  // Notes on the sheet:
  //   JK - FLIP FLOP USING NAND GATES
  //   Q
  //   Q'
endmodule
