// Logisim project 4-1 MUX.circ as structural Verilog: 1 circuit, main circuit main
module main (
  input  D0,
  input  D1,
  input  D2,
  input  D3,
  input  S1,
  input  S0,
  output OUTPUT
);

  wire AND_2_out, AND_3_out, AND_4_out, AND_out, not_1_out, not_2_out;

  not not_1 (not_1_out, S1);
  not not_2 (not_2_out, S0);
  and AND (AND_out, not_1_out, not_2_out, D0);
  and AND_2 (AND_2_out, not_1_out, S0, D1);
  and AND_3 (AND_3_out, S1, not_2_out, D2);
  and AND_4 (AND_4_out, S1, S0, D3);
  or OR (OUTPUT, AND_out, AND_2_out, AND_3_out, AND_4_out);

  // Notes on the sheet:
  //   4 : 1 MULTIPLEXER
endmodule
