// Logisim project Commutative Property_2.circ as structural Verilog: 1 circuit, main circuit main
module main (
  input  A,
  input  B,
  input  B_2,
  input  A_2,
  output A___B,
  output B___A
);

  and AND (A___B, A, B_2);
  and AND_2 (B___A, B, A_2);

  // Notes on the sheet:
  //   LHS
  //   Commutative Property
  //   =
  //   RHS
endmodule
