// Logisim project Distributive Property_1.circ as structural Verilog: 1 circuit, main circuit main
module main (
  input  A,
  input  B,
  input  C,
  input  A_2,
  input  B_2,
  input  C_2,
  output A___BC,
  output A___B___A___C
);

  wire AND_out, OR_2_out, OR_out;

  and AND (AND_out, B, C);
  or OR (OR_out, A_2, B_2);
  or OR_2 (OR_2_out, A_2, C_2);
  or OR_3 (A___BC, A, AND_out);
  and AND_2 (A___B___A___C, OR_out, OR_2_out);

  // Notes on the sheet:
  //   LHS
  //   B
  //   C
  //   RHS
  //   A
  //   BC
  //   A
  //   B
  //   A
  //   C
  //   Distributive Property
  //   A + B
  //   A + C
endmodule
