// Logisim project Distributive Property_2.circ as structural Verilog: 1 circuit, main circuit main
module main (
  input  A,
  input  B,
  input  C,
  input  A_2,
  input  B_2,
  input  C_2,
  output A____B___C,
  output A___B_____A___C
);

  wire AND_2_out, AND_out, OR_out;

  or OR (OR_out, B, C);
  and AND (AND_out, A_2, B_2);
  and AND_2 (AND_2_out, A_2, C_2);
  and AND_3 (A____B___C, A, OR_out);
  or OR_2 (A___B_____A___C, AND_out, AND_2_out);

  // Notes on the sheet:
  //   LHS
  //   B
  //   C
  //   RHS
  //   A
  //   B + C
  //   A
  //   B
  //   A
  //   C
  //   Distributive Property
  //   A . B
  //   A . C
endmodule
